// Logisim project 16bitcpu.circ as structural Verilog
module main (
  input  [15:0] bus_test,
  input  PCtoRAM0ELSE12bitADDR,
  input  add0load1,
  input  clk_enable_pc,
  input  [11:0] addr,
  input  output_enable_enable,
  input  write_enable_enable,
  input  [2:0] outputRegRamALU,
  input  [2:0] write_enable_reg,
  input  [3:0] opcode,
  output [15:0] out_11,
  output [15:0] out_12,
  output [15:0] out_13,
  output [15:0] out_14,
  output Greater_A,
  output Smaller_A,
  output [15:0] out_17,
  output z_flag,
  output [15:0] out_19,
  output c_flag,
  output [15:0] output_CPU,
  output [15:0] out_22
);

  wire and_1_out, clock_1_out, d_ff_1_q, demultiplexer_2_out0, demultiplexer_2_out1, demultiplexer_2_out2,
       demultiplexer_2_out3, demultiplexer_2_out4, demultiplexer_2_out5, demultiplexer_2_out6,
       demultiplexer_2_out7, demultiplexer_3_out0, demultiplexer_3_out1, demultiplexer_3_out2,
       demultiplexer_3_out3, demultiplexer_3_out4, demultiplexer_3_out5, demultiplexer_3_out6,
       multiplexer_2_out, not_1_out, not_2_out, not_4_out, not_5_out, or_2_out, or_3_out, or_4_out, or_5_out,
       or_6_out, or_7_out, or_8_out, or_9_out, or_10_out, or_11_out, or_12_out, or_13_out, or_14_out,
       or_15_out, or_16_out, pull_resistor_1_node;
  wire [11:0] demultiplexer_1_out0, demultiplexer_1_out1, undriven;
  wire [15:0] adder_1_out, and_2_out, demultiplexer_4_out0, divider_1_out, multiplexer_3_out,
       multiplier_1_out, not_3_out, or_1_out, pull_resistor_3_node, subtractor_1_out, xor_1_out;
  wire [15:15] pull_resistor_2_node;

  and and_1 (and_1_out, clock_1_out, not_1_out);
  Clock clock_1 (.out(clock_1_out));
  not not_1 (not_1_out, multiplexer_2_out);
  Intstruction_register intstruction_register_1 (
    .data_bbuss(demultiplexer_4_out0), .write_enabllllle(not_2_out), .clockkkk(and_1_out), .ir_out(out_22));
  registers r0 (
    .data_in(out_11), .write_enable(demultiplexer_2_out0), .clk_in(and_1_out),
    .read_enable(demultiplexer_3_out0), .out_5(out_11));
  registers r1 (
    .data_in(out_11), .write_enable(demultiplexer_2_out1), .clk_in(and_1_out),
    .read_enable(demultiplexer_3_out1), .out_5(out_11));
  registers r2 (
    .data_in(out_11), .write_enable(demultiplexer_2_out2), .clk_in(and_1_out),
    .read_enable(demultiplexer_3_out2), .out_5(out_11));
  registers r3 (
    .data_in(out_11), .write_enable(demultiplexer_2_out3), .clk_in(and_1_out),
    .read_enable(demultiplexer_3_out3), .out_5(out_11));
  registers rA (
    .data_in(out_11), .write_enable(demultiplexer_2_out4), .clk_in(and_1_out), .read_enable(1'b1),
    .out_5(out_14));
  registers rB (
    .data_in(out_11), .write_enable(demultiplexer_2_out5), .clk_in(and_1_out), .read_enable(1'b1),
    .out_5(out_17));
  registers output_register (
    .data_in(out_11), .write_enable(demultiplexer_2_out6), .clk_in(and_1_out), .read_enable(1'b1),
    .out_5(output_CPU));
  Demultiplexer #(.width(12)) demultiplexer_1 (
    .out0(demultiplexer_1_out0), .out1(demultiplexer_1_out1), .in(addr), .sel(demultiplexer_3_out6));
  Demultiplexer #(.select(3)) demultiplexer_2 (
    .out0(demultiplexer_2_out0), .out1(demultiplexer_2_out1), .out2(demultiplexer_2_out2),
    .out3(demultiplexer_2_out3), .out4(demultiplexer_2_out4), .out5(demultiplexer_2_out5),
    .out6(demultiplexer_2_out6), .out7(demultiplexer_2_out7), .in(write_enable_enable), .sel(write_enable_reg));
  Demultiplexer #(.select(3)) demultiplexer_3 (
    .out0(demultiplexer_3_out0), .out1(demultiplexer_3_out1), .out2(demultiplexer_3_out2),
    .out3(demultiplexer_3_out3), .out4(demultiplexer_3_out4), .out5(demultiplexer_3_out5),
    .out6(demultiplexer_3_out6), .in(output_enable_enable), .sel(outputRegRamALU));  // open: out7
  Multiplexer #(.width(16)) multiplexer_1 (.in1(out_19), .out(out_11), .sel(demultiplexer_3_out4));  // open: in0
  Demultiplexer #(.disabled("Z"), .tristate("true"), .width(16)) demultiplexer_4 (
    .out0(demultiplexer_4_out0), .out1(out_11), .in(out_13), .sel(demultiplexer_3_out5));
  Pull_Resistor pull_resistor_1 (.node(pull_resistor_1_node));
  not not_2 (not_2_out, d_ff_1_q);
  program_counter program_counter_1 (
    .data_bus(demultiplexer_1_out1), .load_bus1_add1_0(add0load1), .clockkk(and_1_out),
    .write_enable(clk_enable_pc), .ooutt(out_12));
  Multiplexer #(.select(4)) multiplexer_2 (
    .in0(pull_resistor_1_node), .in1(pull_resistor_1_node), .in2(pull_resistor_1_node),
    .in3(pull_resistor_1_node), .in4(pull_resistor_1_node), .in5(pull_resistor_1_node),
    .in6(pull_resistor_1_node), .in7(pull_resistor_1_node), .in8(pull_resistor_1_node),
    .in9(pull_resistor_1_node), .in10(pull_resistor_1_node), .in11(pull_resistor_1_node),
    .in12(pull_resistor_1_node), .in13(pull_resistor_1_node), .in14(pull_resistor_1_node), .in15(1'b1),
    .out(multiplexer_2_out), .sel(opcode));
  Pull_Resistor pull_resistor_2 (.node(pull_resistor_2_node[15]));
  Adder #(.width(16)) adder_1 (.a(out_14), .b(out_17), .out(adder_1_out), .cout(c_flag));  // open: cin
  Subtractor #(.width(16)) subtractor_1 (.a(out_14), .b(out_17), .out(subtractor_1_out));  // open: bin, bout
  Multiplier #(.width(16)) multiplier_1 (.a(out_14), .b(out_17), .out(multiplier_1_out));  // open: cin, cout
  Divider #(.width(16)) divider_1 (.a(out_14), .b(out_17), .out(divider_1_out));  // open: upper, rem
  assign not_3_out = ~out_14;  // NOT_Gate not_3, 16 bits wide
  assign and_2_out = out_14 & out_17;  // AND_Gate and_2, 16 bits wide
  assign or_1_out = out_14 | out_17;  // OR_Gate or_1, 16 bits wide
  assign xor_1_out = out_14 ^ out_17;  // XOR_Gate xor_1, 16 bits wide
  Comparator #(.mode("unsigned"), .width(16)) comparator_1 (
    .a(out_14), .b(out_17), .gt(Greater_A), .lt(Smaller_A));  // open: eq
  Multiplexer #(.width(16)) multiplexer_3 (
    .in0({{4{pull_resistor_2_node[15]}}, demultiplexer_1_out0}), .in1(out_12), .out(multiplexer_3_out),
    .sel(not_4_out));
  not not_4 (not_4_out, PCtoRAM0ELSE12bitADDR);
  D_Flip_Flop d_ff_1 (.D(not_5_out), .clk(and_1_out), .Q(d_ff_1_q));  // open: Qn, preset, reset
  not not_5 (not_5_out, d_ff_1_q);
  Pull_Resistor pull_resistor_3 (.node(pull_resistor_3_node));
  RAM #(.addrWidth(16), .asyncread("true"), .dataWidth(16)) ram16bit (
    .addr(multiplexer_3_out), .we(demultiplexer_2_out7), .oe(1'b1), .clk(and_1_out), .din(out_11),
    .dout(out_13));
  Multiplexer #(.select(4), .width(16)) multiplexer_4 (
    .in0(adder_1_out), .in1(subtractor_1_out), .in2(multiplier_1_out), .in3(divider_1_out), .in4(not_3_out),
    .in5(and_2_out), .in6(or_1_out), .in7(xor_1_out), .in8(out_14), .in9(out_17),
    .in10(pull_resistor_3_node), .in11(pull_resistor_3_node), .in12(pull_resistor_3_node),
    .in13(pull_resistor_3_node), .in14(pull_resistor_3_node), .in15(pull_resistor_3_node), .out(out_19),
    .sel(opcode));
  or or_2 (or_2_out, or_1_out[0], or_1_out[1]);
  or or_3 (or_3_out, or_1_out[2], or_1_out[3]);
  or or_4 (or_4_out, or_1_out[4], or_1_out[5]);
  or or_5 (or_5_out, or_1_out[6], or_1_out[7]);
  or or_6 (or_6_out, or_1_out[8], or_1_out[9]);
  or or_7 (or_7_out, or_1_out[10], or_1_out[11]);
  or or_8 (or_8_out, or_1_out[12], or_1_out[13]);
  or or_9 (or_9_out, or_1_out[14], or_1_out[15]);
  RAM #(.addrWidth(12), .dataWidth(16)) ram_1 (.addr(undriven));  // open: we, oe, clk, din, dout
  or or_10 (or_10_out, or_2_out, or_3_out);
  or or_11 (or_11_out, or_4_out, or_5_out);
  or or_12 (or_12_out, or_6_out, or_7_out);
  or or_13 (or_13_out, or_8_out, or_9_out);
  or or_14 (or_14_out, or_10_out, or_11_out);
  or or_15 (or_15_out, or_12_out, or_13_out);
  or or_16 (or_16_out, or_14_out, or_15_out);
  not not_6 (z_flag, or_16_out);

  // Notes on the sheet:
  //   Instr_reg0ram
  //   12 bits
  //   12bit to 16bit
  //   SIDDHCESNA - II
endmodule

module mainn (
  input  manual_clk,
  input  [15:0] in_2,
  input  in_3,
  input  in_4,
  input  [15:0] in_5,
  input  in_6,
  input  w_enable_pc,
  input  read_enable_ALU_RAM,
  input  in_9,
  input  [3:0] opcode,
  input  in_11,
  input  [1:0] in_12,
  input  write_enable_ram,
  input  [15:0] in_14,
  output [15:0] out_15,
  output Z,
  output [15:0] outp,
  output C,
  output [1:0] out_19,
  output [1:0] out_20
);

  wire CLOCK_1_out, demultiplexer_1_out0, demultiplexer_1_out1, demultiplexer_2_out0, demultiplexer_2_out1,
       demultiplexer_2_out2, demultiplexer_2_out3, demultiplexer_3_out1, demultiplexer_4_out0,
       demultiplexer_4_out1, demultiplexer_4_out2, demultiplexer_4_out3, demultiplexer_5_out0,
       demultiplexer_5_out1, multiplexer_1_out, not_1_out, not_2_out, or_2_out, or_3_out, or_4_out, or_5_out,
       or_6_out, or_7_out, or_8_out, or_9_out, or_10_out, or_11_out, or_12_out, or_13_out, or_14_out,
       or_15_out, or_16_out;
  wire [1:0] adder_1_out, pull_resistor_2_node, pull_resistor_3_node;
  wire [3:0] demultiplexer_6_out0, demultiplexer_6_out1;
  wire [15:0] adder_2_out, and_1_out, divider_1_out, multiplier_1_out, not_3_out, or_1_out,
       program_counter_1_ooutt, pull_resistor_5_node, ram_1_dout, register_a_out_5, register_b_out_5,
       subtractor_1_out, xor_1_out;

  registers registers_1 (.data_in(in_2), .write_enable(in_3), .clk_in(manual_clk), .read_enable(in_4));  // open: out_5
  Pull_Resistor pull_resistor_1 (.node(in_2));
  Demultiplexer demultiplexer_1 (
    .out0(demultiplexer_1_out0), .out1(demultiplexer_1_out1), .in(read_enable_ALU_RAM), .sel(in_9));
  Multiplexer multiplexer_1 (.in0(demultiplexer_2_out0), .in1(not_1_out), .out(multiplexer_1_out), .sel(out_20[0]));
  not not_1 (not_1_out, demultiplexer_2_out1);
  Demultiplexer #(.select(2)) demultiplexer_2 (
    .out0(demultiplexer_2_out0), .out1(demultiplexer_2_out1), .out2(demultiplexer_2_out2),
    .out3(demultiplexer_2_out3), .in(1'b1), .sel(out_19));
  Demultiplexer #(.select(2)) demultiplexer_3 (
    .out1(demultiplexer_3_out1), .in(1'b1), .sel(out_20));  // open: out0, out2, out3
  Demultiplexer #(.select(2)) demultiplexer_4 (
    .out0(demultiplexer_4_out0), .out1(demultiplexer_4_out1), .out2(demultiplexer_4_out2),
    .out3(demultiplexer_4_out3), .in(in_11), .sel(in_12));
  Demultiplexer demultiplexer_5 (
    .out0(demultiplexer_5_out0), .out1(demultiplexer_5_out1), .in(demultiplexer_3_out1), .sel(not_2_out));
  not not_2 (not_2_out, multiplexer_1_out);
  Register #(.width(2)) register_1 (.D(adder_1_out), .en(1'b1), .clk(CLOCK_1_out), .Q(out_20));  // open: clr
  Adder #(.width(2)) adder_1 (.a(out_20), .b(2'b01), .out(adder_1_out));  // open: cin, cout
  main main_1 ();  // open: bus_test, PCtoRAM0ELSE12bitADDR, add0load1, clk_enable_pc, addr, output_enable_enable, write_enable_enable, outputRegRamALU, write_enable_reg, opcode, out_11, out_12, out_13, out_14, Greater_A, Smaller_A, out_17, z_flag, out_19, c_flag, output_CPU, out_22
  Clock CLOCK_1 (.out(CLOCK_1_out));
  Multiplexer #(.select(2), .width(2)) multiplexer_2 (
    .in0(in_14[10:9]), .in1(in_14[8:7]), .in2(pull_resistor_2_node), .in3(pull_resistor_3_node),
    .out(out_19), .sel(out_20));
  Pull_Resistor pull_resistor_2 (.node(pull_resistor_2_node));
  Pull_Resistor pull_resistor_3 (.node(pull_resistor_3_node));
  Demultiplexer #(.width(4)) demultiplexer_6 (
    .out0(demultiplexer_6_out0), .out1(demultiplexer_6_out1), .in(in_14[14:11]), .sel(in_14[15]));
  registers R_0 (
    .data_in(in_5), .write_enable(demultiplexer_4_out0), .clk_in(CLOCK_1_out),
    .read_enable(demultiplexer_2_out0), .out_5(in_5));
  registers R_1 (
    .data_in(in_5), .write_enable(demultiplexer_4_out1), .clk_in(CLOCK_1_out),
    .read_enable(demultiplexer_2_out1), .out_5(in_5));
  registers R_2 (
    .data_in(in_5), .write_enable(demultiplexer_4_out2), .clk_in(CLOCK_1_out),
    .read_enable(demultiplexer_2_out2), .out_5(in_5));
  registers R_3 (
    .data_in(in_5), .write_enable(demultiplexer_4_out3), .clk_in(CLOCK_1_out),
    .read_enable(demultiplexer_2_out3), .out_5(in_5));
  registers register_a (
    .data_in(in_5), .write_enable(demultiplexer_5_out0), .clk_in(CLOCK_1_out), .read_enable(1'b1),
    .out_5(register_a_out_5));
  registers register_b (
    .data_in(in_5), .write_enable(demultiplexer_5_out1), .clk_in(CLOCK_1_out), .read_enable(1'b1),
    .out_5(register_b_out_5));
  Pull_Resistor pull_resistor_4 (.node(in_5));
  Multiplexer #(.width(16)) multiplexer_3 (.in1(outp), .out(in_5), .sel(demultiplexer_1_out0));  // open: in0
  Multiplexer #(.width(16)) multiplexer_4 (.in1(ram_1_dout), .out(in_5), .sel(demultiplexer_1_out1));  // open: in0
  main main_2 ();  // open: bus_test, PCtoRAM0ELSE12bitADDR, add0load1, clk_enable_pc, addr, output_enable_enable, write_enable_enable, outputRegRamALU, write_enable_reg, opcode, out_11, out_12, out_13, out_14, Greater_A, Smaller_A, out_17, z_flag, out_19, c_flag, output_CPU, out_22
  program_counter program_counter_1 (
    .data_bus(in_5[11:0]), .load_bus1_add1_0(in_6), .clockkk(CLOCK_1_out), .write_enable(w_enable_pc),
    .ooutt(program_counter_1_ooutt));
  Adder #(.width(16)) adder_2 (.a(register_a_out_5), .b(register_b_out_5), .out(adder_2_out), .cout(C));  // open: cin
  Subtractor #(.width(16)) subtractor_1 (
    .a(register_a_out_5), .b(register_b_out_5), .out(subtractor_1_out));  // open: bin, bout
  Multiplier #(.width(16)) multiplier_1 (
    .a(register_a_out_5), .b(register_b_out_5), .out(multiplier_1_out));  // open: cin, cout
  Divider #(.width(16)) divider_1 (
    .a(register_a_out_5), .b(register_b_out_5), .out(divider_1_out));  // open: upper, rem
  assign not_3_out = ~register_a_out_5;  // NOT_Gate not_3, 16 bits wide
  assign and_1_out = register_a_out_5 & register_b_out_5;  // AND_Gate and_1, 16 bits wide
  assign or_1_out = register_a_out_5 | register_b_out_5;  // OR_Gate or_1, 16 bits wide
  assign xor_1_out = register_a_out_5 ^ register_b_out_5;  // XOR_Gate xor_1, 16 bits wide
  Pull_Resistor pull_resistor_5 (.node(pull_resistor_5_node));
  RAM #(.addrWidth(16), .dataWidth(16)) ram_1 (
    .addr(program_counter_1_ooutt), .we(write_enable_ram), .oe(1'b1), .clk(CLOCK_1_out), .din(in_5),
    .dout(ram_1_dout));
  Multiplexer #(.select(4), .width(16)) multiplexer_5 (
    .in0(adder_2_out), .in1(subtractor_1_out), .in2(multiplier_1_out), .in3(divider_1_out), .in4(not_3_out),
    .in5(and_1_out), .in6(or_1_out), .in7(xor_1_out), .in8(register_a_out_5), .in9(register_b_out_5),
    .in10(pull_resistor_5_node), .in11(pull_resistor_5_node), .in12(pull_resistor_5_node),
    .in13(pull_resistor_5_node), .in14(pull_resistor_5_node), .in15(pull_resistor_5_node), .out(outp),
    .sel(opcode));
  or or_2 (or_2_out, or_1_out[0], or_1_out[1]);
  or or_3 (or_3_out, or_1_out[2], or_1_out[3]);
  or or_4 (or_4_out, or_1_out[4], or_1_out[5]);
  or or_5 (or_5_out, or_1_out[6], or_1_out[7]);
  or or_6 (or_6_out, or_1_out[8], or_1_out[9]);
  or or_7 (or_7_out, or_1_out[10], or_1_out[11]);
  or or_8 (or_8_out, or_1_out[12], or_1_out[13]);
  or or_9 (or_9_out, or_1_out[14], or_1_out[15]);
  or or_10 (or_10_out, or_2_out, or_3_out);
  or or_11 (or_11_out, or_4_out, or_5_out);
  or or_12 (or_12_out, or_6_out, or_7_out);
  or or_13 (or_13_out, or_8_out, or_9_out);
  or or_14 (or_14_out, or_10_out, or_11_out);
  or or_15 (or_15_out, or_12_out, or_13_out);
  or or_16 (or_16_out, or_14_out, or_15_out);
  not not_4 (Z, or_16_out);
  // Pins of 12 and 16 bits meet at in_5

  assign out_15 = in_5;

  // Notes on the sheet:
  //   0 for w enable of A and B respectively
endmodule

module registers (
  input  [15:0] data_in,
  input  write_enable,
  input  clk_in,
  input  read_enable,
  output [15:0] out_5
);

  wire [15:0] register_1_q, undriven;

  Register #(.width(16)) register_1 (.D(data_in), .en(write_enable), .clk(clk_in), .Q(register_1_q));  // open: clr
  Multiplexer #(.width(16)) multiplexer_1 (.in0(undriven), .in1(register_1_q), .out(out_5), .sel(read_enable));
endmodule

module program_counter (
  input  [11:0] data_bus,
  input  load_bus1_add1_0,
  input  clockkk,
  input  write_enable,
  output [15:0] ooutt
);

  wire and_1_out;
  wire [15:0] adder_1_out, multiplexer_1_out;
  wire [15:15] pull_resistor_1_node;

  Pull_Resistor pull_resistor_1 (.node(pull_resistor_1_node[15]));
  Multiplexer #(.width(16)) multiplexer_1 (
    .in0(adder_1_out), .in1({{4{pull_resistor_1_node[15]}}, data_bus}), .out(multiplexer_1_out),
    .sel(load_bus1_add1_0));
  and and_1 (and_1_out, clockkk, write_enable);
  D_Flip_Flop d_ff_1 (.D(multiplexer_1_out[15]), .clk(and_1_out), .Q(ooutt[15]));  // open: Qn, preset, reset
  D_Flip_Flop d_ff_2 (.D(multiplexer_1_out[14]), .clk(and_1_out), .Q(ooutt[14]));  // open: Qn, preset, reset
  D_Flip_Flop d_ff_3 (.D(multiplexer_1_out[13]), .clk(and_1_out), .Q(ooutt[13]));  // open: Qn, preset, reset
  D_Flip_Flop d_ff_4 (.D(multiplexer_1_out[12]), .clk(and_1_out), .Q(ooutt[12]));  // open: Qn, preset, reset
  D_Flip_Flop d_ff_5 (.D(multiplexer_1_out[11]), .clk(and_1_out), .Q(ooutt[11]));  // open: Qn, preset, reset
  D_Flip_Flop d_ff_6 (.D(multiplexer_1_out[10]), .clk(and_1_out), .Q(ooutt[10]));  // open: Qn, preset, reset
  D_Flip_Flop d_ff_7 (.D(multiplexer_1_out[9]), .clk(and_1_out), .Q(ooutt[9]));  // open: Qn, preset, reset
  D_Flip_Flop d_ff_8 (.D(multiplexer_1_out[8]), .clk(and_1_out), .Q(ooutt[8]));  // open: Qn, preset, reset
  D_Flip_Flop d_ff_9 (.D(multiplexer_1_out[7]), .clk(and_1_out), .Q(ooutt[7]));  // open: Qn, preset, reset
  D_Flip_Flop d_ff_10 (.D(multiplexer_1_out[6]), .clk(and_1_out), .Q(ooutt[6]));  // open: Qn, preset, reset
  D_Flip_Flop d_ff_11 (.D(multiplexer_1_out[5]), .clk(and_1_out), .Q(ooutt[5]));  // open: Qn, preset, reset
  D_Flip_Flop d_ff_12 (.D(multiplexer_1_out[4]), .clk(and_1_out), .Q(ooutt[4]));  // open: Qn, preset, reset
  Adder #(.width(16)) adder_1 (.a(ooutt), .b(16'h1), .out(adder_1_out));  // open: cin, cout
  D_Flip_Flop d_ff_13 (.D(multiplexer_1_out[3]), .clk(and_1_out), .Q(ooutt[3]));  // open: Qn, preset, reset
  D_Flip_Flop d_ff_14 (.D(multiplexer_1_out[2]), .clk(and_1_out), .Q(ooutt[2]));  // open: Qn, preset, reset
  D_Flip_Flop d_ff_15 (.D(multiplexer_1_out[1]), .clk(and_1_out), .Q(ooutt[1]));  // open: Qn, preset, reset
  D_Flip_Flop d_ff_16 (.D(multiplexer_1_out[0]), .clk(and_1_out), .Q(ooutt[0]));  // open: Qn, preset, reset
endmodule

module ALU (
  input  [15:0] A,
  input  [15:0] B,
  input  [3:0] opcode,
  output Z,
  output [15:0] outp,
  output C
);

  wire or_2_out, or_3_out, or_4_out, or_5_out, or_6_out, or_7_out, or_8_out, or_9_out, or_10_out, or_11_out,
       or_12_out, or_13_out, or_14_out, or_15_out, or_16_out;
  wire [15:0] adder_1_out, and_1_out, divider_1_out, multiplier_1_out, not_1_out, or_1_out,
       pull_resistor_1_node, subtractor_1_out, xor_1_out;

  Adder #(.width(16)) adder_1 (.a(A), .b(B), .out(adder_1_out), .cout(C));  // open: cin
  Subtractor #(.width(16)) subtractor_1 (.a(A), .b(B), .out(subtractor_1_out));  // open: bin, bout
  Multiplier #(.width(16)) multiplier_1 (.a(A), .b(B), .out(multiplier_1_out));  // open: cin, cout
  Divider #(.width(16)) divider_1 (.a(A), .b(B), .out(divider_1_out));  // open: upper, rem
  assign not_1_out = ~A;  // NOT_Gate not_1, 16 bits wide
  assign and_1_out = A & B;  // AND_Gate and_1, 16 bits wide
  assign or_1_out = A | B;  // OR_Gate or_1, 16 bits wide
  assign xor_1_out = A ^ B;  // XOR_Gate xor_1, 16 bits wide
  Pull_Resistor pull_resistor_1 (.node(pull_resistor_1_node));
  Multiplexer #(.select(4), .width(16)) multiplexer_1 (
    .in0(adder_1_out), .in1(subtractor_1_out), .in2(multiplier_1_out), .in3(divider_1_out), .in4(not_1_out),
    .in5(and_1_out), .in6(or_1_out), .in7(xor_1_out), .in8(A), .in9(B), .in10(pull_resistor_1_node),
    .in11(pull_resistor_1_node), .in12(pull_resistor_1_node), .in13(pull_resistor_1_node),
    .in14(pull_resistor_1_node), .in15(pull_resistor_1_node), .out(outp), .sel(opcode));
  or or_2 (or_2_out, or_1_out[0], or_1_out[1]);
  or or_3 (or_3_out, or_1_out[2], or_1_out[3]);
  or or_4 (or_4_out, or_1_out[4], or_1_out[5]);
  or or_5 (or_5_out, or_1_out[6], or_1_out[7]);
  or or_6 (or_6_out, or_1_out[8], or_1_out[9]);
  or or_7 (or_7_out, or_1_out[10], or_1_out[11]);
  or or_8 (or_8_out, or_1_out[12], or_1_out[13]);
  or or_9 (or_9_out, or_1_out[14], or_1_out[15]);
  or or_10 (or_10_out, or_2_out, or_3_out);
  or or_11 (or_11_out, or_4_out, or_5_out);
  or or_12 (or_12_out, or_6_out, or_7_out);
  or or_13 (or_13_out, or_8_out, or_9_out);
  or or_14 (or_14_out, or_10_out, or_11_out);
  or or_15 (or_15_out, or_12_out, or_13_out);
  or or_16 (or_16_out, or_14_out, or_15_out);
  not not_2 (Z, or_16_out);
endmodule

module control_unit (
  input  [15:0] in_1
);

  wire [3:0] demultiplexer_1_out0;

  Demultiplexer #(.width(4)) demultiplexer_1 (
    .out0(demultiplexer_1_out0), .in(in_1[14:11]), .sel(in_1[15]));  // open: out1
endmodule

module state_register (
  input  clckck,
  output [1:0] out_2
);

  wire [1:0] adder_1_out;

  Register #(.width(2)) register_1 (.D(adder_1_out), .en(1'b1), .clk(clckck), .Q(out_2));  // open: clr
  Adder #(.width(2)) adder_1 (.a(out_2), .b(2'b01), .out(adder_1_out));  // open: cin, cout
endmodule

module Intstruction_register (
  input  [15:0] data_bbuss,
  input  write_enabllllle,
  input  clockkkk,
  output [15:0] ir_out
);

  Register #(.width(16)) register_1 (.D(data_bbuss), .en(write_enabllllle), .clk(clockkkk), .Q(ir_out));  // open: clr
endmodule
